# Fritzing sketch Circuit_Sketch_Fritzing (saved by Fritzing 0.9.4)
breadboards: 1

parts:
  Mod2 = Raspberry Pi Pico
  S1 = Pushbutton [package="[SMD]"]
  S2 = Pushbutton [package="[SMD]"]
  LED1 = LED - 5mm [color="Blue (430nm)" package="5 mm [THT]"]
  LED2 = LED - 5mm [color="Green (555nm)" package="5 mm [THT]"]
  LED3 = LED - 5mm [color="Red (633nm)" package="5 mm [THT]"]
  R1 = Resistor [tolerance=±5% resistance=100 package=THT]
  R2 = Resistor [tolerance=±5% resistance=100 package=THT]
  R3 = Resistor [tolerance=±5% resistance=100 package=THT]

nets:
  N1: Mod2.pin_3, Mod2.pin_8, Mod2.pin_13, Mod2.pin_18, Mod2.pin_23, Mod2.pin_28, Mod2.pin_33, Mod2.pin_38, Mod2.pin_42, S1.Pin_3, S1.Pin_4, S2.Pin_3, S2.Pin_4, LED1.cathode, LED2.cathode, LED3.cathode
  N2: Mod2.pin_17, R3.Pin_1
  N3: Mod2.pin_19, S2.Pin_1, S2.Pin_2
  N4: Mod2.pin_21, R1.Pin_1
  N5: Mod2.pin_22, R2.Pin_1
  N6: Mod2.pin_24, S1.Pin_1, S1.Pin_2
  N7: LED1.anode, R3.Pin_0
  N8: LED2.anode, R2.Pin_0
  N9: LED3.anode, R1.Pin_0

custom parts:
  Raspberry Pi Pico: Raspberry Pi Pico. Based around the RP2040 microcontroller the Pico is a low cost microcontroller device bringing Raspberry Pi quality, cost, and easy of use to the microcontroller space. Jan 2021, Split part in to two versions: tht (this one) and SMD. This one will drill holes for a .1 in header in pcb to allow plugging in the module as well as providing pads to solder the module to the top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
